# Fritzing sketch sketch (saved by Fritzing 0.9.3b)
breadboards: 1

parts:
  LED1 = smd LED [color="Red (633nm)" package="0603 [SMD]"]
  R1 = PHOTOCELL [package=photocell]
  Raspberry_Pi1 = Raspberry Pi B+
  hc-sr1 = hc-sr04

nets:
  GND: LED1.cathode, R1.P$2, Raspberry_Pi1.GPIO4, Raspberry_Pi1.GND, Raspberry_Pi1.GPIO16, Raspberry_Pi1.GPIO18, hc-sr1.Trig, hc-sr1.GND
  N1: LED1.anode, R1.P$1
  N2: Raspberry_Pi1.GPIO17, Raspberry_Pi1.GPIO27, hc-sr1.Echo
  5V: Raspberry_Pi1.5V, hc-sr1.VCC
